# Fritzing sketch Diagrama_esquematico_termometro_RGB_05102016 (saved by Fritzing 0.9.2b)

parts:
  Digispark = Digispark [part_number=ATtiny85]
  Neopixel = ws2812b [part_number=WS2812b package="smd 2812b"]
  R2 = Resistor [tolerance=±5% resistance=10k package="0603 [SMD]"]
  R1_-_10k = Temperature Sensor (Thermistor) [thermistor_type=NTC package=THT]

nets:
  VCC: Digispark.VCC, Neopixel.VDD, R1_-_10k.pin_1
  GND: Digispark.GND, Neopixel.VSS, R2.Pin_0
  N1: Digispark.P0, Neopixel.DIN
  N2: Digispark.P2, R1_-_10k.pin_0

custom parts:
  Digispark: The Digispark is an Attiny85 based microcontroller development board similar to the Arduino line, only cheaper, smaller, and a bit less powerful. With a whole host of shields to extend its functionality and the ability to use the familiar Arduino IDE the Digispark is a great way to jump into electronics, or perfect for when an Arduino is too big or too much.
